# Fritzing sketch sketch (saved by Fritzing 1.0.6)
breadboards: 1

parts:
  Mod1 = Amica NodeMCU DEVKIT 1.0
  Mod2 = KY-004 Key Switch Module [package="Breakout board"]
  Part1 = LCD1602-I2C
  Mod3 = KY-009 Full Color RGB LED SMD Module [package="Breakout board"]
  LED1 = LED - 5mm [color="Yellow (595nm)" current=0.030A package="5 mm [THT]"]
  R1 = Rotary Potentiometer (Small) [maximum_resistance=100kΩ knob_status=50% power=0.5W package=THT]
  Mod4 = KY-015 Temperature & Humidity Sensor Module [package="Breakout board"]
  R2 = Resistor [tolerance=±5% resistance=220 package="1206 [SMD]"]
  Mod5 = KY-004 Key Switch Module [package="Breakout board"]
  R3 = Resistor [tolerance=±5% resistance=10k package="1206 [SMD]"]

nets:
  VCC: Mod1.pin1, Mod1.pin_10, Mod1.pin_26, Part1.VCC, R1.leg1, Mod4.Vin, Mod4.-, R2.Pin_1, R3.Pin_1
  N1: Mod1.pin2, Mod1.pin_9, Mod1.pin_25, Mod1.pin_29, Mod2.-, Part1.GND, Mod3.-, R1.leg2, Mod5.-
  N2: Mod1.pin5, Mod3.B
  N3: Mod1.pin6, Mod3.R
  N4: Mod1.pin7, Mod2.S
  N5: Mod1.pin8, LED1.cathode
  N6: Mod1.pin_12, Mod4.S
  N7: Mod1.pin_13, Part1.SDA
  N8: Mod1.pin_14, Part1.SCL
  N9: Mod1.pin_16, R1.wiper
  N10: Mod1.pin_28, Mod5.S, R3.Pin_0
  N11: LED1.anode, R2.Pin_0

custom parts:
  KY-004 Key Switch Module: Arduino Key Switch Module Keyes KY-004 is a push button that will output a high signal when pressed.
  LCD1602-I2C: A standard character display, usually with 2x16 characters. Comes in many colors with LCM1602 IIC attached.
  KY-009 Full Color RGB LED SMD Module: KY-009 RGB full color LED Module, emits a range of colors by mixing red, green and blue light. The amount of each color is adjusted using PWM.
  KY-015 Temperature & Humidity Sensor Module: KY-015 temperature and humidity sensor module, provides a low-latency serial interface to measure humidity and temperature.

// code stored in the sketch: sketch.fzz.ino

